# Fritzing sketch final_homework (saved by Fritzing 1.0.3b)
breadboards: 2

parts:
  Mod1 = Raspberry Pi Pico W
  buz1 = Piezo Buzzer
  LED1 = RGB LED (com. cathode, rgb) [color="Red (633nm)" current=0.030A package="5 mm [THT]"]
  LED2 = LED - 3mm [color="Red (633nm)" current=0.030A package="3 mm [THT]"]
  S1 = Momentary Switch [package=ksa_sealed_tac_switch]
  HC-SR04_Sensor_1 = HC-SR04 Ultrasonic Distance Sensor
  LCD1 = LCD screen
  J1 = Basic Servo
  U1 = POT [knob_status=50% power=0.5W package=alps_pot]
  U2 = POT [knob_status=50% power=0.5W package=alps_pot]
  R1 = Resistor [tolerance=±5% power=0.25W resistance=220 package=THT]
  R2 = Resistor [tolerance=±5% power=0.25W resistance=220 package=THT]
  R3 = Resistor [tolerance=±5% power=0.25W resistance=220 package=THT]
  R4 = Resistor [tolerance=±5% power=0.25W resistance=220 package=THT]
  R5 = Resistor [tolerance=±5% power=0.25W resistance=10k package=THT]
  R6 = Resistor [tolerance=±5% power=0.25W resistance=1k package=THT]

nets:
  N1: Mod1.pin_1, LCD1.RS
  N2: Mod1.pin_2, LCD1.E
  GND: Mod1.pin_3, Mod1.pin_8, Mod1.pin_13, Mod1.pin_18, Mod1.pin_23, Mod1.pin_28, Mod1.pin_33, Mod1.pin_38, buz1.pin_2, LED1.common_cathode, LED2.cathode, HC-SR04_Sensor_1.GND, LCD1.VSS, LCD1.R/W, LCD1.LED-, J1.gnd, U1.A, U2.A, R5.Pin_1
  N3: Mod1.pin_4, LCD1.DB4
  N4: Mod1.pin_5, LCD1.DB5
  N5: Mod1.pin_6, LCD1.DB6
  N6: Mod1.pin_7, LCD1.DB7
  N7: Mod1.pin_9, R1.Pin_1
  N8: Mod1.pin_10, R3.Pin_1
  N9: Mod1.pin_11, R2.Pin_1
  N10: Mod1.pin_12, buz1.pin_1
  N11: Mod1.pin_14, HC-SR04_Sensor_1.TRIG
  N12: Mod1.pin_15, R6.Pin_1
  N13: Mod1.pin_16, J1.pulse
  N14: Mod1.pin_17, S1.1, R5.Pin_0
  N15: Mod1.pin_19, R4.Pin_1
  N16: Mod1.pin_31, U1.S
  N17: Mod1.pin_32, LCD1.V0, U2.S
  VCC: Mod1.pin_36, S1.4, HC-SR04_Sensor_1.VCC, LCD1.LED+, J1.vcc, U1.E, U2.E
  N18: Mod1.pin_40, LCD1.VDD
  N19: LED1.red_anode, R1.Pin_0
  N20: LED1.green_anode, R3.Pin_0
  N21: LED1.blue_anode, R2.Pin_0
  N22: LED2.anode, R4.Pin_0
  N23: HC-SR04_Sensor_1.ECHO, R6.Pin_0

custom parts:
  Raspberry Pi Pico W: Raspberry Pi Pico W. Based around the RP2040 microcontroller the Pico W is a low cost microcontroller device bringing Raspberry Pi quality, cost, and easy of use to the microcontroller space. The areas marked KEEPOUT in pcb silkscreen should not have traces running through them to avoid shorts on a soldered in module!
  Piezo Buzzer: Part from https://www.nutsvolts.com/magazine/article/november2012_SmileysWorkshop. Breadboard and icon images modified to be 0.3" in spacing and be more similar to the actual physical part.
